// Logisim project cache.circ as structural Verilog: 1 circuit, main circuit cache
module cache (
  input  [31:0] data_in,
  input  [1:0] word_index,
  input  CLOCK,
  input  RESET
);

  // B_lock b_lock_1: pin names not known
  // B_lock b_lock_2: pin names not known
  // B_lock b_lock_3: pin names not known
  // B_lock b_lock_4: pin names not known
  // B_lock b_lock_5: pin names not known
  // B_lock b_lock_6: pin names not known
  // B_lock b_lock_7: pin names not known
  // B_lock b_lock_8: pin names not known

  // Notes on the sheet:
  //   set1
  //   set2
  //   se3
  //   se4
endmodule
