// Logisim project cpu.circ as structural Verilog: 1 circuit, main circuit cpu
module cpu (
);

  wire ALU_main_zero, ALU_v, ALUSrc, and_1_out, Branch, clock_1_out, Jump, MemToReg, RegDst, RegWrite;
  wire [3:0] MemWriteMask;
  wire [4:0] instSplitter_rd, instSplitter_rs, instSplitter_rt, instSplitter_shamt, mux2_y;
  wire [5:0] ALU_op, instSplitter_func, instSplitter_op;
  wire [15:0] instSplitter_imm16;
  wire [25:0] instSplitter_target26;
  wire [27:0] SXL_2_t28;
  wire [31:0] Adder1_result, Adder_result, ALU_main_aluresult, DataMem_memreaddata, InstMem_memreaddata,
       mux1_y, mux3_y, mux4_y, mux_y, PC_pc_out, RegisterFile_readdata1, RegisterFile_readdata2, SE_s32,
       SHL2_y;

  Clock clock_1 (.out(clock_1_out));
  ProgramCounter PC (.PC_in(mux_y), .PC_out(PC_pc_out));
  Adder_32bit Adder (.A(PC_pc_out), .B(32'h4), .Result(Adder_result));
  mem InstMem (
    .MemAddress(PC_pc_out), .clk(clock_1_out), .MemReadData(InstMem_memreaddata));  // open: MemWriteMask, MemWriteData
  mux2x32 mux (.x0(mux1_y), .x1({Adder_result[31:28], SXL_2_t28}), .Sel(Jump), .Y(mux_y));
  SXL2 SXL_2 (.T26(instSplitter_target26), .T28(SXL_2_t28));
  instruction_splitter instSplitter (
    .instruction(InstMem_memreaddata), .op(instSplitter_op), .target26(instSplitter_target26),
    .rs(instSplitter_rs), .rt(instSplitter_rt), .imm16(instSplitter_imm16), .rd(instSplitter_rd),
    .shamt(instSplitter_shamt), .func(instSplitter_func));
  mux2x32 mux1 (.x0(Adder_result), .x1(Adder1_result), .Sel(and_1_out), .Y(mux1_y));
  CU ControlUnit (
    .Func(instSplitter_func), .Opcode(instSplitter_op), .ALUSrc(ALUSrc), .ALUop(ALU_op), .RegDst(RegDst),
    .ALU_V(ALU_v), .MemToReg(MemToReg), .RegWrite(RegWrite), .MemWriteMask(MemWriteMask), .Branch(Branch),
    .Jump(Jump));
  mux2x5 mux2 (.X0(instSplitter_rt), .X1(instSplitter_rd), .Sel(RegDst), .Y(mux2_y));
  SignExtend SE (.S16(instSplitter_imm16), .S32(SE_s32));
  regfile RegisterFile (
    .ReadIndex1(instSplitter_rs), .ReadIndex2(instSplitter_rt), .WriteIndex(mux2_y), .WriteData(mux4_y),
    .RegWEn(RegWrite), .clk(clock_1_out), .ReadData1(RegisterFile_readdata1),
    .ReadData2(RegisterFile_readdata2));
  mux2x32 mux3 (.x0(RegisterFile_readdata2), .x1(SE_s32), .Sel(ALUSrc), .Y(mux3_y));
  shiftLeffBy2 SHL2 (.in_1(SE_s32), .Y(SHL2_y));
  Adder_32bit Adder1 (.A(Adder_result), .B(SHL2_y), .Result(Adder1_result));
  ALU ALU_main (
    .A(RegisterFile_readdata1), .B(mux3_y), .ALUOp(ALU_op), .Func(instSplitter_func), .Imm(SE_s32),
    .Shamt(instSplitter_shamt), .ALUSrc(ALUSrc), .Zero(ALU_main_zero), .ALUResult(ALU_main_aluresult));
  and and_1 (and_1_out, Branch, ALU_main_zero);
  mem DataMem (
    .MemAddress(ALU_main_aluresult), .MemWriteMask(MemWriteMask), .MemWriteData(RegisterFile_readdata2),
    .clk(clock_1_out), .MemReadData(DataMem_memreaddata));
  mux2x32 mux4 (.x0(ALU_main_aluresult), .x1(DataMem_memreaddata), .Sel(MemToReg), .Y(mux4_y));
endmodule
